# Fritzing sketch temperature-controller (saved by Fritzing 0.9.2b)
breadboards: 1

parts:
  Arduino_Nano_Atmega328P = Arduino Nano v2.3
  Q1 = Basic FET N-Channel [package="TO220 [THT]"]
  D1 = Rectifier Diode [part_number=1N4001 package="300 mil [THT]"]
  V1 = DC Power [voltage=12V]
  R2 = Resistor [tolerance=±5% resistance=220 package=THT]
  R3 = Resistor [tolerance=±5% resistance=10k package=THT]
  T1 = LM35 Temperature Sensor [package="TO92 [THT]"]
  T2 = LM35 Temperature Sensor [package="TO92 [THT]"]
  C1 = Electrolytic Capacitor [capacitance=1µF package="100 mil [THT, electrolytic]"]
  C2 = Electrolytic Capacitor [capacitance=1µF package="100 mil [THT, electrolytic]"]
  R4 = Resistor [tolerance=±5% resistance=75 package=THT]
  R5 = Resistor [tolerance=±5% resistance=75 package=THT]
  JP9 = Header 3 [package=jst-3-pth]

nets:
  GND: Arduino_Nano_Atmega328P.GND, Q1.source, V1.V-, R3.Pin_1, T1.GND, T2.GND, C1.-, C2.-
  N1: Arduino_Nano_Atmega328P.D9, R2.Pin_0
  N2: Arduino_Nano_Atmega328P.A1, T2.Vout, R5.Pin_1
  N3: Arduino_Nano_Atmega328P.A0, T1.Vout, R4.Pin_1
  N4: Arduino_Nano_Atmega328P.+5V, T1.+Vs, T2.+Vs
  N5: Q1.gate, R2.Pin_1, R3.Pin_0
  N6: Q1.drain, D1.anode, JP9.1
  N7: D1.cathode, V1.V+, JP9.2
  N8: C1.+, R5.Pin_0
  N9: C2.+, R4.Pin_0

notes:
  12V from XL6009 step-up converter (using 5V from Arduino)
